# Fritzing sketch spritelet2-protrinket (saved by Fritzing 0.9.2b)
circuit board: 4.318cm x 4.445cm

parts:
  J1 = female pin header, 11 pins [form="♀ (female)"]
  VS = female pin header, 2 pins [form="♀ (female)"]
  J4 = female pin header, 2 pins [form="♀ (female)"]
  J5 = female pin header, 3 pins [form="♀ (female)"]
  RT = female pin header, 1 pin [form="♀ (female)"]
  LT = female pin header, 1 pin [form="♀ (female)"]
  J2 = female pin header, 12 pins [form="♀ (female)"]
  J3 = female pin header, 12 pins [form="♀ (female)"]
  POWER = Toggle Switch [package=THT]
  UP = female pin header, 1 pin [form="♀ (female)"]
  DN = female pin header, 1 pin [form="♀ (female)"]
  CT = female pin header, 1 pin [form="♀ (female)"]
  CM = female pin header, 1 pin [form="♀ (female)"]

nets:
  N1: J1.pin1, J5.pin1, J3.pin1
  N2: J1.pin3, J5.pin2, J3.pin2
  N3: J1.pin4, J2.pin5
  N4: J1.pin5, J2.pin4
  N5: J1.pin6, J2.pin3
  N6: J1.pin7, J2.pin2
  N7: J1.pin8, J3.pin6
  N8: J1.pin9, J3.pin5
  N9: J1.pin10, J3.pin7
  N10: J1.pin11, J2.pin1
  N11: VS.pin1, J3.pin8
  N12: VS.pin2, J3.pin9
  N13: J4.pin1, POWER.L2
  N14: J4.pin2, POWER.COM
  N15: J5.pin3, J3.pin3
  N16: RT.pin1, J2.pin12
  N17: LT.pin1, J2.pin11
  N18: J2.pin7, CM.pin1
  N19: J2.pin8, CT.pin1
  N20: J2.pin9, UP.pin1
  N21: J2.pin10, DN.pin1

notes:
  USB Side
  FTDI Side
  < Adafruit Pro Trinket >
  Adafruit
  LiPoly
  Backpack
  /\
  \/
  < Adafruit 1.44" TFT Backpack >
  SLET-TRKT-B
