# Fritzing sketch spritelet2-teensy (saved by Fritzing 0.9.2b)
circuit board: 4.318cm x 4.445cm

parts:
  VS = female pin header, 2 pins [form="♀ (female)"]
  J4 = female pin header, 2 pins [form="♀ (female)"]
  J5 = female pin header, 3 pins [form="♀ (female)"]
  RT = female pin header, 1 pin [form="♀ (female)"]
  CT = female pin header, 1 pin [form="♀ (female)"]
  LT = female pin header, 1 pin [form="♀ (female)"]
  UP = female pin header, 1 pin [form="♀ (female)"]
  DN = female pin header, 1 pin [form="♀ (female)"]
  CM = female pin header, 1 pin [form="♀ (female)"]
  POWER = Toggle Switch [package=THT]
  J7 = female pin header, 14 pins [form="♀ (female)"]
  J1 = female pin header, 11 pins [form="♀ (female)"]
  J8 = female pin header, 3 pins [form="♀ (female)"]
  J9 = female pin header, 4 pins [form="♀ (female)"]
  J10 = female pin header, 5 pins [form="♀ (female)"]
  J11 = female pin header, 1 pin [form="♀ (female)"]

nets:
  N1: VS.pin1, J9.pin2
  N2: VS.pin2, J9.pin1
  N3: J4.pin1, POWER.L2
  N4: J4.pin2, POWER.COM
  N5: J5.pin1, J7.pin1, J1.pin1
  N6: J5.pin2, J7.pin2, J1.pin3, J8.pin1
  N7: J5.pin3, J11.pin1
  N8: RT.pin1, J7.pin11
  N9: CT.pin1, J7.pin8
  N10: LT.pin1, J7.pin10
  N11: UP.pin1, J7.pin9
  N12: DN.pin1, J7.pin12
  N13: CM.pin1, J7.pin13
  N14: J7.pin14, J1.pin4
  N15: J1.pin5, J10.pin5
  N16: J1.pin6, J10.pin4
  N17: J1.pin7, J10.pin3
  N18: J1.pin8, J10.pin2
  N19: J1.pin9, J10.pin1
  N20: J1.pin10, J9.pin4
  N21: J1.pin11, J9.pin3

notes:
  USB Side
  Pin Side
  < Teensy 3.x/LC >
  Adafruit
  LiPoly
  Backpack
  /\
  \/
  < Adafruit 1.44" TFT Backpack >
  SLET-TNSY-B
